// Logisim project mux.circ as structural Verilog: 1 circuit, main circuit main
module main (
);

  wire adder_1_cout, adder_2_cout, adder_3_cout, adder_4_cout, adder_5_cout, adder_6_cout, adder_9_cout,
       adder_10_cout, adder_11_cout, adder_12_p1, adder_12_p5, adder_13_cout, adder_14_cout, adder_15_cout,
       adder_16_cout, adder_17_cout, adder_18_cout, adder_19_cout, adder_20_cout, adder_21_cout,
       adder_22_cout, and_1_out, multiplexer_1_out, multiplexer_2_out, multiplexer_3_out, multiplexer_4_out,
       multiplexer_5_out, multiplexer_6_out, multiplexer_7_out, multiplexer_8_out, multiplexer_9_out,
       nor_1_out, nor_2_out, nor_3_out, not_1_out, undriven, undriven_2, undriven_3, undriven_4, undriven_5,
       undriven_6, undriven_7, undriven_8, undriven_9, undriven_10, undriven_11, undriven_12, undriven_13,
       undriven_14, undriven_15, undriven_16, undriven_37, undriven_45, undriven_46, undriven_47,
       undriven_48, undriven_49, undriven_50, undriven_51, xnor_1_out, xnor_2_out, xnor_3_out, xnor_4_out,
       xnor_5_out, xor_1_out, xor_2_out;
  wire [1:0] undriven_38, undriven_39, undriven_40, undriven_41, undriven_42, undriven_43, undriven_44;
  wire [7:0] adder_1_out, adder_2_out, adder_3_out, adder_4_out, adder_5_out, adder_6_out, adder_7_cout,
       adder_7_out, adder_8_cout, adder_8_out, adder_9_out, adder_10_out, adder_11_out, adder_13_out,
       adder_14_out, adder_15_out, adder_16_out, adder_17_out, adder_18_out, adder_19_out, adder_20_out,
       adder_21_out, adder_22_out, S00_out, S01_out, S02_out, S10_out, S11_out, S12_out, S20_out, S21_out,
       S22_out, undriven_17, undriven_18, undriven_19, undriven_20, undriven_21, undriven_22, undriven_23,
       undriven_24, undriven_25, undriven_26, undriven_27, undriven_28, undriven_29, undriven_30,
       undriven_31, undriven_32, undriven_33, undriven_34, undriven_35, undriven_36;
  wire [7:1] adder_12_p3;

  and S20 (S20_out[0], undriven, undriven_4);
  and S21 (S21_out[0], undriven_2, undriven_4);
  and S22 (S22_out[0], undriven_3, undriven_4);
  and S10 (S10_out[0], undriven, undriven_5);
  and S11 (S11_out[0], undriven_2, undriven_5);
  and S12 (S12_out[0], undriven_3, undriven_5);
  and S00 (S00_out[0], undriven, undriven_6);
  and S01 (S01_out[0], undriven_2, undriven_6);
  and S02 (S02_out[0], undriven_3, undriven_6);
  Adder adder_1 (.a({adder_12_p3, 1'b0}), .b(S00_out), .out(adder_1_out), .cin(1'b0), .cout(adder_1_cout));
  Adder adder_2 (.a({adder_12_p3, 1'b0}), .b(S10_out), .out(adder_2_out), .cin(1'b0), .cout(adder_2_cout));
  Adder adder_3 (.a({adder_12_p3, 1'b0}), .b(S20_out), .out(adder_3_out), .cin(1'b0), .cout(adder_3_cout));
  Adder adder_4 (.a(adder_2_out), .b(S01_out), .out(adder_4_out), .cin(adder_1_cout), .cout(adder_4_cout));
  Adder adder_5 (.a(adder_3_out), .b(S11_out), .out(adder_5_out), .cin(adder_2_cout), .cout(adder_5_cout));
  Adder adder_6 (.a(S21_out), .b({adder_12_p3, 1'b0}), .out(adder_6_out), .cin(adder_3_cout), .cout(adder_6_cout));
  Adder adder_7 (.a(adder_5_out), .b(S02_out), .out(adder_7_out), .cin(adder_4_cout), .cout(adder_7_cout[0]));
  Adder adder_8 (.a(adder_6_out), .b(S12_out), .out(adder_8_out), .cin(adder_5_cout), .cout(adder_8_cout[0]));
  Adder adder_9 (.a({adder_12_p3, 1'b0}), .b(S22_out), .out(adder_9_out), .cin(adder_6_cout), .cout(adder_9_cout));
  xnor xnor_1 (xnor_1_out, undriven_7, undriven_8);
  xnor xnor_2 (xnor_2_out, undriven_9, undriven_10);
  xnor xnor_3 (xnor_3_out, undriven_11, undriven_12);
  xnor xnor_4 (xnor_4_out, undriven_13, undriven_14);
  xnor xnor_5 (xnor_5_out, undriven_15, undriven_16);
  Adder adder_10 (.a(adder_7_cout), .b(adder_8_out), .out(adder_10_out), .cin(1'b0), .cout(adder_10_cout));
  Adder adder_11 (.a(adder_8_cout), .b(adder_9_out), .out(adder_11_out), .cin(adder_10_cout), .cout(adder_11_cout));
  // Adder adder_12: pin names not known; wires that end beside it: adder_12_p1, adder_9_cout, {adder_12_p3, 1'b0}, adder_11_cout, adder_12_p5
  Adder adder_13 (.a(undriven_17), .b(undriven_18), .out(adder_13_out), .cin(adder_12_p1), .cout(adder_13_cout));
  Adder adder_14 (.a(undriven_19), .b(undriven_20), .out(adder_14_out), .cin(adder_13_cout), .cout(adder_14_cout));
  Adder adder_15 (.a(undriven_21), .b(undriven_22), .out(adder_15_out), .cin(adder_14_cout), .cout(adder_15_cout));
  Adder adder_16 (.a(undriven_23), .b(undriven_24), .out(adder_16_out), .cin(adder_15_cout), .cout(adder_16_cout));
  Adder adder_17 (.a(undriven_25), .b(undriven_26), .out(adder_17_out), .cin(adder_16_cout), .cout(adder_17_cout));
  Adder adder_18 (.a(undriven_27), .b(undriven_28), .out(adder_18_out), .cin(undriven_37), .cout(adder_18_cout));
  Adder adder_19 (.a(undriven_29), .b(undriven_30), .out(adder_19_out), .cin(adder_18_cout), .cout(adder_19_cout));
  Adder adder_20 (.a(undriven_31), .b(undriven_32), .out(adder_20_out), .cin(adder_19_cout), .cout(adder_20_cout));
  Adder adder_21 (.a(undriven_33), .b(undriven_34), .out(adder_21_out), .cin(adder_20_cout), .cout(adder_21_cout));
  Adder adder_22 (.a(undriven_35), .b(undriven_36), .out(adder_22_out), .cin(adder_21_cout), .cout(adder_22_cout));
  and and_1 (and_1_out, xnor_1_out, xnor_2_out, xnor_3_out, xnor_4_out, xnor_5_out);
  not not_1 (not_1_out, and_1_out);
  xor xor_1 (xor_1_out, adder_16_cout, adder_17_cout);
  xor xor_2 (xor_2_out, adder_21_cout, adder_22_cout);
  nor nor_1 (nor_1_out, adder_13_out[0], adder_14_out[0], adder_15_out[0], adder_16_out[0], adder_17_out[0]);
  nor nor_2 (nor_2_out, adder_18_out[0], adder_19_out[0], adder_20_out[0], adder_21_out[0], adder_22_out[0]);
  nor nor_3 (nor_3_out, adder_1_out[0], adder_4_out[0], adder_7_out[0], adder_10_out[0], adder_11_out[0]);
  Multiplexer #(.select(2)) multiplexer_1 (
    .in0(1'b0), .in1(1'b0), .in2(adder_17_out[0]), .in3(adder_22_out[0]), .out(multiplexer_1_out),
    .sel(undriven_38), .en(undriven_45));
  Multiplexer #(.select(2)) multiplexer_2 (
    .in0(1'b0), .in1(1'b0), .in2(xor_1_out), .in3(xor_2_out), .out(multiplexer_2_out), .sel(undriven_39),
    .en(undriven_46));
  Multiplexer #(.select(2)) multiplexer_3 (
    .in0(1'b1), .in1(nor_3_out), .in2(nor_1_out), .in3(nor_2_out), .out(multiplexer_3_out),
    .sel(undriven_40), .en(undriven_47));
  Multiplexer #(.select(2)) multiplexer_4 (
    .in0(not_1_out), .in1(adder_12_p5), .in2(adder_17_cout), .in3(adder_22_cout), .out(multiplexer_4_out),
    .sel(undriven_41), .en(undriven_48));
  Multiplexer #(.select(2)) multiplexer_5 (
    .in0(1'b0), .in1(adder_1_out[0]), .in2(adder_13_out[0]), .in3(adder_18_out[0]), .out(multiplexer_5_out),
    .sel(undriven_42), .en(undriven_49));
  Multiplexer #(.select(2)) multiplexer_6 (
    .in0(1'b0), .in1(adder_4_out[0]), .in2(adder_14_out[0]), .in3(adder_19_out[0]), .out(multiplexer_6_out),
    .sel(undriven_43), .en(undriven_50));
  Multiplexer #(.select(2)) multiplexer_7 (
    .in0(1'b0), .in1(adder_7_out[0]), .in2(adder_15_out[0]), .in3(adder_20_out[0]), .out(multiplexer_7_out),
    .sel(undriven_44), .en(undriven_51));
  Multiplexer #(.select(2)) multiplexer_8 (
    .in0(1'b0), .in1(adder_10_out[0]), .in2(adder_16_out[0]), .in3(adder_21_out[0]), .out(multiplexer_8_out),
    .sel(undriven_44), .en(undriven_51));
  Multiplexer #(.select(2)) multiplexer_9 (
    .in0(1'b0), .in1(adder_11_out[0]), .in2(adder_17_out[0]), .in3(adder_22_out[0]), .out(multiplexer_9_out),
    .sel(undriven_44), .en(undriven_51));
  // Pins of 1 and 8 bits meet at {adder_12_p3, 1'b0}
  // Pins of 1 and 8 bits meet at S00_out
  // Pins of 1 and 8 bits meet at adder_1_out
  // Pins of 1 and 8 bits meet at adder_13_out
  // Pins of 1 and 8 bits meet at adder_15_out
  // Pins of 1 and 8 bits meet at S01_out
  // Pins of 1 and 8 bits meet at S20_out
  // Pins of 1 and 8 bits meet at adder_17_out
  // Pins of 1 and 8 bits meet at adder_16_out
  // Pins of 1 and 8 bits meet at adder_7_cout
  // Pins of 1 and 8 bits meet at adder_10_out
  // Pins of 1 and 8 bits meet at S22_out

  // Notes on the sheet:
  //   a4
  //   b1
  //   b2
  //   b3
  //   a3
  //   a2
  //   a0
  //   b0
  //   a1
  //   b1
  //   a2
  //   b2
  //   a3
  //   b3
  //   a4
  //   b4
  //   0
  //   a0
  //   b1
  //   a1
  //   b2
  //   a2
  //   b3
  //   a3
  //   0
  //   a4
  //   0
  //   1
  //   a0
  //   b0
  //   a1
  //   b1
  //   a2
  //   b2
  //   a3
  //   b3
  //   a4
  //   b4
  //   f0
  //   f1
  //   f2
  //   f3
  //   f4
  //   f0
  //   f1
  //   f2
  //   f3
  //   f4
  //   Cout
  //   Negative
  //   Cout
  //   Negative
  //   Cout
  //   Zero
  //   Overflow
  //   Zero
  //   Overflow
  //   0
  //   f0
  //   f1
  //   f2
  //   f3
  //   f4
  //   Zero
  //   Cout
  //   1
  //   S0
  //   S1
  //   NEGATIVE
  //   OVERFLOW
  //   ZERO
  //   Cout
  //   F0
  //   F1
  //   F2
  //   F3
  //   F4
endmodule
