// Logisim project s00.circ as structural Verilog: 1 circuit, main circuit main
module main (
);

  wire adder_1_cout, adder_1_out, adder_2_cout, adder_2_out, adder_3_cout, adder_3_out, adder_4_cout,
       adder_4_out, adder_5_out, adder_6_out, adder_7_out, adder_8_out, adder_9_cout, adder_9_out, and_1_out,
       and_2_out, and_3_out, and_4_out, and_5_out, and_6_out, and_7_out, and_8_out, and_9_out, nor_1_out,
       undriven, undriven_2, undriven_3, undriven_4, undriven_5, undriven_6, undriven_7, undriven_8,
       undriven_9, undriven_10, undriven_11, undriven_12;

  and and_1 (and_1_out, undriven, undriven_4);
  and and_2 (and_2_out, undriven_2, undriven_4);
  and and_3 (and_3_out, undriven_3, undriven_4);
  and and_4 (and_4_out, undriven, undriven_5);
  and and_5 (and_5_out, undriven_2, undriven_5);
  and and_6 (and_6_out, undriven_3, undriven_5);
  and and_7 (and_7_out, undriven, undriven_6);
  and and_8 (and_8_out, undriven_2, undriven_6);
  and and_9 (and_9_out, undriven_3, undriven_6);
  Adder #(.width(1)) adder_1 (.a(and_7_out), .b(undriven_7), .out(adder_1_out), .cin(undriven_9), .cout(adder_1_cout));
  Adder #(.width(1)) adder_2 (.a(and_4_out), .b(and_8_out), .out(adder_2_out), .cin(adder_1_cout), .cout(adder_2_cout));
  Adder #(.width(1)) adder_3 (.a(and_1_out), .b(and_5_out), .out(adder_3_out), .cin(adder_2_cout), .cout(adder_3_cout));
  Adder #(.width(1)) adder_4 (
    .a(undriven_8), .b(and_2_out), .out(adder_4_out), .cin(adder_3_cout), .cout(adder_4_cout));
  Adder #(.width(1)) adder_5 (.a(adder_1_out), .b(undriven_10), .out(adder_5_out), .cin(undriven_12));  // open: cout
  Adder #(.width(1)) adder_6 (.a(adder_2_out), .b(undriven_11), .out(adder_6_out));  // open: cin, cout
  Adder #(.width(1)) adder_7 (.a(adder_3_out), .b(and_9_out), .out(adder_7_out));  // open: cin, cout
  Adder #(.width(1)) adder_8 (.a(adder_4_out), .b(and_6_out), .out(adder_8_out));  // open: cin, cout
  Adder #(.width(1)) adder_9 (.a(adder_4_cout), .b(and_3_out), .out(adder_9_out), .cout(adder_9_cout));  // open: cin
  nor nor_1 (nor_1_out, adder_5_out, adder_6_out, adder_7_out, adder_8_out, adder_9_out);

  // Notes on the sheet:
  //   a4
  //   b1
  //   b2
  //   b3
  //   a3
  //   a2
  //   Overflow
  //   Negative
  //   0
  //   0
  //   0
  //   0
  //   0
  //   0
  //   f0
  //   f1
  //   f2
  //   f3
  //   f4
  //   Cout
  //   Zero
endmodule
