// Logisim project s01.circ as structural Verilog: 1 circuit, main circuit main
module main (
);

  wire and_1_out, not_1_out, undriven, undriven_2, undriven_3, undriven_4, undriven_5, undriven_6,
       undriven_7, undriven_8, undriven_9, undriven_10, xnor_1_out, xnor_2_out, xnor_3_out, xnor_4_out,
       xnor_5_out;

  xnor xnor_1 (xnor_1_out, undriven, undriven_2);
  xnor xnor_2 (xnor_2_out, undriven_3, undriven_4);
  xnor xnor_3 (xnor_3_out, undriven_5, undriven_6);
  xnor xnor_4 (xnor_4_out, undriven_7, undriven_8);
  xnor xnor_5 (xnor_5_out, undriven_9, undriven_10);
  and and_1 (and_1_out, xnor_1_out, xnor_2_out, xnor_3_out, xnor_4_out, xnor_5_out);
  not not_1 (not_1_out, and_1_out);

  // Notes on the sheet:
  //   a0
  //   b0
  //   Zero
  //   F
  //   Overflow
  //   a1
  //   Negative
  //   b1
  //   a2
  //   b2
  //   a3
  //   b3
  //   a4
  //   b4
  //   Cout
endmodule
