// Logisim project s11.circ as structural Verilog: 1 circuit, main circuit main
module main (
);

  wire adder_1_cout, adder_2_cout, adder_3_cout, adder_4_cout, adder_5_cout, nor_1_out, undriven_11,
       xor_1_out;
  wire [7:0] adder_1_out, adder_2_out, adder_3_out, adder_4_out, adder_5_out, undriven, undriven_2,
       undriven_3, undriven_4, undriven_5, undriven_6, undriven_7, undriven_8, undriven_9, undriven_10;

  Adder adder_1 (.a(undriven), .b(undriven_2), .out(adder_1_out), .cin(undriven_11), .cout(adder_1_cout));
  Adder adder_2 (.a(undriven_3), .b(undriven_4), .out(adder_2_out), .cin(adder_1_cout), .cout(adder_2_cout));
  Adder adder_3 (.a(undriven_5), .b(undriven_6), .out(adder_3_out), .cin(adder_2_cout), .cout(adder_3_cout));
  Adder adder_4 (.a(undriven_7), .b(undriven_8), .out(adder_4_out), .cin(adder_3_cout), .cout(adder_4_cout));
  Adder adder_5 (.a(undriven_9), .b(undriven_10), .out(adder_5_out), .cin(adder_4_cout), .cout(adder_5_cout));
  xor xor_1 (xor_1_out, adder_4_cout, adder_5_cout);
  nor nor_1 (nor_1_out, adder_1_out[0], adder_2_out[0], adder_3_out[0], adder_4_out[0], adder_5_out[0]);
  // Pins of 1 and 8 bits meet at adder_4_out
  // Pins of 1 and 8 bits meet at adder_5_out
  // Pins of 1 and 8 bits meet at adder_1_out
  // Pins of 1 and 8 bits meet at adder_3_out
  // Pins of 1 and 8 bits meet at adder_2_out

  // Notes on the sheet:
  //   1
  //   a0
  //   b0
  //   a1
  //   b1
  //   a2
  //   b2
  //   a3
  //   b3
  //   a4
  //   b4
  //   f0
  //   f1
  //   f2
  //   f3
  //   f4
  //   Negative
  //   Cout
  //   Zero
  //   Overflow
endmodule
